# Fritzing sketch ADXL345 (saved by Fritzing 0.9.3b)

parts:
  Raspberry_Pi1 = Raspberry Pi 2
  Part2 = Triple Axis Accelerometer Breakout - ADXL345

nets:
  3V3: Raspberry_Pi1.3v3, Part2.VCC
  N1: Raspberry_Pi1.GPIO2, Part2.SDA
  N2: Raspberry_Pi1.GPIO3, Part2.SCL
  GND: Raspberry_Pi1.GND, Part2.GND
