# Fritzing sketch 3 LEDs (saved by Fritzing 0.9.3b)
breadboards: 1

parts:
  Raspberry_Pi1 = Raspberry Pi 2
  LED1 = smd LED [color="Red (633nm)" package="1206 [SMD]"]
  LED2 = smd LED [color="Green (555nm)" package="1206 [SMD]"]
  LED3 = smd LED [color="Blue (525nm)" package="1206 [SMD]"]

nets:
  N1: Raspberry_Pi1.GND, LED1.cathode, LED2.cathode, LED3.cathode
  N2: Raspberry_Pi1.GPIO24, LED2.anode
  N3: Raspberry_Pi1.GPIO23, LED3.anode
  N4: Raspberry_Pi1.GPIO18, LED1.anode
